// Logisim project Arqui.circ as structural Verilog: 11 circuits, main circuit main
module main (
  input  ON_OFF,
  input  [2:0] x,
  input  [2:0] y,
  output [3:0] out_4
);

  wire clock_1_out, flipflopd_1_out_6, flipflopd_1_out_7, flipflopd_1_out_13, logica_clock_1_out_4,
       logicaestados_1_out_5, logicaestados_1_out_6, logicaestados_1_out_7;
  wire [4:0] flipflopd_1_out_12, logicaestados_1_out_4;

  logicaEstados logicaestados_1 (
    .in_1(x), .in_2(y), .in_3(flipflopd_1_out_12), .out_4(logicaestados_1_out_4),
    .out_5(logicaestados_1_out_5), .out_6(logicaestados_1_out_6), .out_7(logicaestados_1_out_7));
  Clock clock_1 (.out(clock_1_out));
  Logica_clock logica_clock_1 (
    .in_2(clock_1_out), .out_4(logica_clock_1_out_4), .in_1(flipflopd_1_out_13), .in_3(logicaestados_1_out_5));
  FlipFlopD flipflopd_1 (
    .in_4(logica_clock_1_out_4), .in_5(logicaestados_1_out_4), .out_13(flipflopd_1_out_13),
    .in_1(logicaestados_1_out_6), .F(logicaestados_1_out_7), .out_6(flipflopd_1_out_6),
    .out_7(flipflopd_1_out_7), .out_8(flipflopd_1_out_12[4]), .out_9(flipflopd_1_out_12[3]),
    .out_10(flipflopd_1_out_12[2]), .out_11(flipflopd_1_out_12[1]), .out_12(flipflopd_1_out_12[0]),
    .in_2(ON_OFF));
  salida salida_1 (.A(logicaestados_1_out_5), .B(flipflopd_1_out_6), .C(flipflopd_1_out_7), .out_4(out_4));
endmodule

module direccion (
  input  [4:0] in_1,
  output complete,
  output dir,
  output s
);

  wire and_2_out, and_3_out, and_4_out, and_5_out, and_6_out, and_7_out, and_8_out, and_9_out, and_10_out,
       and_11_out, and_12_out, and_13_out, and_14_out, not_1_out, not_2_out, not_3_out, not_4_out, not_5_out,
       not_6_out, not_7_out, not_8_out, not_9_out, not_10_out, not_11_out, not_12_out, not_13_out,
       not_14_out, not_15_out, not_16_out, not_17_out, not_18_out, not_19_out, not_20_out, not_21_out,
       not_22_out, not_23_out, not_24_out, not_25_out, not_26_out, not_27_out, not_28_out;

  not not_1 (not_1_out, in_1[4]);
  not not_2 (not_2_out, in_1[0]);
  not not_3 (not_3_out, in_1[3]);
  not not_4 (not_4_out, in_1[1]);
  not not_5 (not_5_out, in_1[0]);
  not not_6 (not_6_out, in_1[4]);
  not not_7 (not_7_out, in_1[1]);
  not not_8 (not_8_out, in_1[0]);
  not not_9 (not_9_out, in_1[3]);
  not not_10 (not_10_out, in_1[1]);
  not not_11 (not_11_out, in_1[4]);
  not not_12 (not_12_out, in_1[3]);
  not not_13 (not_13_out, in_1[4]);
  not not_14 (not_14_out, in_1[2]);
  not not_15 (not_15_out, in_1[1]);
  not not_16 (not_16_out, in_1[2]);
  not not_17 (not_17_out, in_1[0]);
  not not_18 (not_18_out, in_1[0]);
  not not_19 (not_19_out, in_1[4]);
  not not_20 (not_20_out, in_1[2]);
  not not_21 (not_21_out, in_1[1]);
  not not_22 (not_22_out, in_1[4]);
  not not_23 (not_23_out, in_1[2]);
  not not_24 (not_24_out, in_1[3]);
  not not_25 (not_25_out, in_1[1]);
  not not_26 (not_26_out, in_1[0]);
  not not_27 (not_27_out, in_1[4]);
  not not_28 (not_28_out, in_1[2]);
  and and_1 (complete, not_1_out, in_1[3], in_1[2], in_1[1], not_2_out);
  and and_2 (and_2_out, not_3_out, not_4_out, not_5_out);
  and and_3 (and_3_out, not_6_out, in_1[2], not_7_out, not_8_out);
  and and_4 (and_4_out, not_9_out, in_1[2], not_10_out);
  and and_5 (and_5_out, not_11_out, not_12_out, in_1[2], in_1[0]);
  and and_6 (and_6_out, not_13_out, in_1[3], not_14_out, not_15_out, in_1[0]);
  and and_7 (and_7_out, in_1[4], in_1[3], not_16_out, not_17_out);
  and and_8 (and_8_out, in_1[4], in_1[3], in_1[1], not_18_out);
  and and_9 (and_9_out, not_19_out, in_1[0]);
  and and_10 (and_10_out, not_20_out, not_21_out, in_1[0]);
  and and_11 (and_11_out, not_22_out, not_23_out, in_1[1]);
  and and_12 (and_12_out, not_24_out, in_1[2], not_25_out, not_26_out);
  and and_13 (and_13_out, not_27_out, in_1[3], not_28_out);
  and and_14 (and_14_out, in_1[4], in_1[2], in_1[1]);
  or or_1 (dir, and_2_out, and_3_out, and_4_out, and_5_out, and_6_out, and_7_out, and_8_out);
  or or_2 (s, and_9_out, and_10_out, and_11_out, and_12_out, and_13_out, and_14_out);
endmodule

module FlipFlopD (
  input  in_1,
  input  in_2,
  input  F,
  input  in_4,
  input  [4:0] in_5,
  output out_6,
  output out_7,
  output out_8,
  output out_9,
  output out_10,
  output out_11,
  output out_12,
  output out_13
);

  wire A, A_prime, and_1_out, and_2_out, and_3_out, and_4_out, and_5_out, and_6_out, and_7_out, and_8_out,
       and_9_out, and_10_out, and_11_out, and_12_out, and_13_out, and_14_out, and_15_out, and_16_out,
       and_17_out, and_18_out, and_19_out, and_20_out, B, B_prime, C, C_prime, D, D_prime, E, E_prime,
       ff_d_1_not_q, ff_d_2_not_q, ff_d_3_not_q, ff_d_4_not_q, ff_d_5_not_q, not_1_out, not_2_out, not_3_out,
       not_4_out, not_5_out, not_6_out, not_7_out, not_8_out, not_9_out;
  wire [4:0] registro_1_out_4;

  registro registro_1 (.in_1(in_4), .out_4(registro_1_out_4), .in_2(in_5), .in_3(in_2));
  Multiplexer #(.width(5), .enable("false")) multiplexer_1 (
    .in0({E, D, C, B, A}), .in1(in_5), .out({E_prime, D_prime, C_prime, B_prime, A_prime}), .sel(out_13));
  Comparar comparar_1 (.in_1(in_5), .in_2(registro_1_out_4), .out_3(out_13));
  FF_D ff_d_1 (.D(E_prime), .Q(out_8), .Not_Q(ff_d_1_not_q), .Clk(in_4), .in_3(in_2));
  FF_D ff_d_2 (.D(D_prime), .Q(out_9), .Not_Q(ff_d_2_not_q), .Clk(in_4), .in_3(in_2));
  FF_D ff_d_3 (.D(C_prime), .Q(out_10), .Not_Q(ff_d_3_not_q), .Clk(in_4), .in_3(in_2));
  FF_D ff_d_4 (.D(B_prime), .Q(out_11), .Not_Q(ff_d_4_not_q), .Clk(in_4), .in_3(in_2));
  FF_D ff_d_5 (.D(A_prime), .Q(out_12), .Not_Q(ff_d_5_not_q), .Clk(in_4), .in_3(in_2));
  and and_1 (and_1_out, out_8, out_11);
  and and_2 (and_2_out, out_8, out_9);
  and and_3 (and_3_out, F, out_8);
  not not_1 (not_1_out, in_1);
  not not_2 (not_2_out, F);
  not not_3 (not_3_out, in_1);
  not not_4 (not_4_out, F);
  not not_5 (not_5_out, in_1);
  not not_6 (not_6_out, in_1);
  not not_7 (not_7_out, F);
  not not_8 (not_8_out, in_1);
  not not_9 (not_9_out, F);
  or or_1 (E, and_1_out, and_2_out, and_3_out);
  and and_4 (and_4_out, not_1_out, out_9);
  and and_5 (and_5_out, ff_d_1_not_q, out_9);
  and and_6 (and_6_out, in_1, out_10, out_11);
  and and_7 (and_7_out, in_1, not_2_out, out_8, ff_d_2_not_q);
  and and_8 (and_8_out, not_3_out, not_4_out, ff_d_4_not_q, out_12);
  and and_9 (and_9_out, ff_d_1_not_q, ff_d_3_not_q, out_11, out_12);
  and and_10 (and_10_out, not_5_out, ff_d_2_not_q, out_10);
  and and_11 (and_11_out, ff_d_1_not_q, out_10, ff_d_4_not_q);
  and and_12 (and_12_out, in_1, out_9, ff_d_5_not_q);
  and and_13 (and_13_out, in_1, out_8, ff_d_3_not_q);
  and and_14 (and_14_out, not_6_out, ff_d_1_not_q, ff_d_2_not_q, ff_d_5_not_q);
  and and_15 (and_15_out, ff_d_1_not_q, ff_d_4_not_q, out_12);
  and and_16 (and_16_out, not_7_out, ff_d_2_not_q, out_10);
  and and_17 (and_17_out, out_8, ff_d_4_not_q, ff_d_5_not_q);
  and and_18 (and_18_out, out_8, out_11, out_12);
  and and_19 (and_19_out, not_8_out, F, ff_d_1_not_q, ff_d_3_not_q, out_11, ff_d_5_not_q);
  and and_20 (and_20_out, not_9_out, ff_d_3_not_q, ff_d_4_not_q);
  or or_2 (A, and_20_out, ff_d_5_not_q);
  or or_3 (D, and_4_out, and_5_out, and_6_out, and_7_out);
  or or_4 (C, and_8_out, and_9_out, and_10_out, and_11_out, and_12_out, and_13_out);
  or or_5 (B, and_14_out, and_15_out, and_16_out, and_17_out, and_18_out, and_19_out);

  assign out_6 = in_1;
  assign out_7 = F;
endmodule

module Coordenada_Codificacion (
  input  [2:0] cordenada_Y,
  input  [2:0] cordenada_X,
  output out_3,
  output out_4,
  output out_5,
  output out_6,
  output out_7
);

  wire and_1_out, and_2_out, and_3_out, and_4_out, and_5_out, and_6_out, and_7_out, and_8_out, and_9_out,
       and_10_out, and_11_out, and_12_out, and_13_out, and_14_out, and_15_out, and_16_out, and_17_out,
       and_18_out, and_19_out, and_20_out, and_21_out, and_22_out, and_23_out, and_24_out, and_25_out,
       and_26_out, not_1_out, not_2_out, not_3_out, not_4_out, not_5_out, not_6_out, not_7_out, not_8_out,
       not_9_out, not_10_out, not_11_out, not_12_out, not_13_out, not_14_out, not_15_out, not_16_out,
       not_17_out, not_18_out, not_19_out, not_20_out, not_21_out, not_22_out, not_23_out, not_24_out,
       not_25_out, not_26_out, not_27_out, not_28_out, not_29_out, not_30_out, not_31_out, not_32_out,
       not_33_out, not_34_out;

  not not_1 (not_1_out, cordenada_Y[2]);
  not not_2 (not_2_out, cordenada_Y[2]);
  not not_3 (not_3_out, cordenada_X[2]);
  not not_4 (not_4_out, cordenada_Y[1]);
  not not_5 (not_5_out, cordenada_Y[0]);
  not not_6 (not_6_out, cordenada_Y[2]);
  not not_7 (not_7_out, cordenada_X[1]);
  not not_8 (not_8_out, cordenada_X[0]);
  not not_9 (not_9_out, cordenada_Y[0]);
  not not_10 (not_10_out, cordenada_X[2]);
  not not_11 (not_11_out, cordenada_X[0]);
  not not_12 (not_12_out, cordenada_Y[2]);
  not not_13 (not_13_out, cordenada_Y[1]);
  not not_14 (not_14_out, cordenada_Y[2]);
  not not_15 (not_15_out, cordenada_Y[0]);
  not not_16 (not_16_out, cordenada_Y[0]);
  not not_17 (not_17_out, cordenada_X[2]);
  not not_18 (not_18_out, cordenada_X[0]);
  not not_19 (not_19_out, cordenada_Y[2]);
  not not_20 (not_20_out, cordenada_X[2]);
  not not_21 (not_21_out, cordenada_Y[1]);
  not not_22 (not_22_out, cordenada_Y[0]);
  not not_23 (not_23_out, cordenada_Y[0]);
  not not_24 (not_24_out, cordenada_Y[2]);
  not not_25 (not_25_out, cordenada_X[1]);
  not not_26 (not_26_out, cordenada_Y[0]);
  not not_27 (not_27_out, cordenada_X[1]);
  not not_28 (not_28_out, cordenada_X[0]);
  not not_29 (not_29_out, cordenada_Y[2]);
  not not_30 (not_30_out, cordenada_Y[0]);
  not not_31 (not_31_out, cordenada_X[1]);
  not not_32 (not_32_out, cordenada_X[2]);
  not not_33 (not_33_out, cordenada_Y[0]);
  not not_34 (not_34_out, cordenada_X[0]);
  and and_1 (and_1_out, not_1_out, cordenada_X[2], cordenada_X[0]);
  and and_2 (and_2_out, not_2_out, cordenada_X[2], cordenada_X[1]);
  and and_3 (and_3_out, cordenada_Y[2], cordenada_Y[0], not_3_out);
  and and_4 (and_4_out, cordenada_Y[2], cordenada_Y[1]);
  and and_5 (and_5_out, not_4_out, not_5_out);
  and and_6 (and_6_out, cordenada_Y[2], cordenada_X[2], cordenada_X[1]);
  and and_7 (and_7_out, cordenada_Y[2], cordenada_Y[0], cordenada_X[2]);
  and and_8 (and_8_out, cordenada_Y[2], cordenada_Y[1], cordenada_Y[0]);
  and and_9 (and_9_out, not_6_out, not_7_out, not_8_out);
  and and_10 (and_10_out, not_9_out, not_10_out, not_11_out);
  and and_11 (and_11_out, not_12_out, not_13_out, cordenada_X[2]);
  and and_12 (and_12_out, not_14_out, cordenada_Y[1], cordenada_Y[0]);
  and and_13 (and_13_out, cordenada_Y[2], cordenada_X[2], cordenada_X[1]);
  and and_14 (and_14_out, cordenada_Y[2], cordenada_Y[1], not_15_out);
  and and_15 (and_15_out, not_16_out, not_17_out, not_18_out);
  and and_16 (and_16_out, not_19_out, not_20_out, cordenada_X[1]);
  and and_17 (and_17_out, not_21_out, not_22_out, cordenada_X[2], cordenada_X[0]);
  and and_18 (and_18_out, cordenada_Y[1], not_23_out, cordenada_X[1]);
  and and_19 (and_19_out, not_24_out, cordenada_Y[1], cordenada_Y[0]);
  and and_20 (and_20_out, cordenada_Y[2], cordenada_Y[0], cordenada_X[2], not_25_out);
  and and_21 (and_21_out, not_26_out, not_27_out, not_28_out);
  and and_22 (and_22_out, not_29_out, not_30_out, cordenada_X[2], cordenada_X[0]);
  and and_23 (and_23_out, cordenada_X[2], not_31_out, cordenada_X[0]);
  and and_24 (and_24_out, cordenada_Y[0], not_32_out, cordenada_X[0]);
  and and_25 (and_25_out, cordenada_Y[2], not_33_out, not_34_out);
  and and_26 (and_26_out, cordenada_Y[2], cordenada_Y[0], cordenada_X[0]);
  or or_1 (out_3, and_1_out, and_2_out, and_3_out, and_4_out);
  or or_2 (out_4, and_5_out, and_6_out, and_7_out, and_8_out);
  or or_3 (out_5, and_9_out, and_10_out, and_11_out, and_12_out, and_13_out, and_14_out);
  or or_4 (out_6, and_15_out, and_16_out, and_17_out, and_18_out, and_19_out, and_20_out);
  or or_5 (out_7, and_21_out, and_22_out, and_23_out, and_24_out, and_25_out, and_26_out);
endmodule

module backup (
  input  C1,
  input  B1,
  input  A1,
  input  C2,
  input  B2,
  input  A2,
  output e,
  output d,
  output c,
  output b,
  output a
);

  wire and_1_out, and_2_out, and_3_out, and_4_out, and_5_out, and_6_out, and_7_out, and_8_out, and_9_out,
       and_10_out, and_11_out, and_12_out, and_13_out, and_14_out, and_15_out, and_16_out, and_17_out,
       and_18_out, and_19_out, and_20_out, and_21_out, and_22_out, and_23_out, and_24_out, and_25_out,
       and_26_out, not_1_out, not_2_out, not_3_out, not_4_out, not_5_out, not_6_out, not_7_out, not_8_out,
       not_9_out, not_10_out, not_11_out, not_12_out, not_13_out, not_14_out, not_15_out, not_16_out,
       not_17_out, not_18_out, not_19_out, not_20_out, not_21_out, not_22_out, not_23_out, not_24_out,
       not_25_out, not_26_out, not_27_out, not_28_out, not_29_out, not_30_out, not_31_out, not_32_out,
       not_33_out, not_34_out;

  not not_1 (not_1_out, C1);
  not not_2 (not_2_out, C1);
  not not_3 (not_3_out, C2);
  not not_4 (not_4_out, B1);
  not not_5 (not_5_out, A1);
  not not_6 (not_6_out, C1);
  not not_7 (not_7_out, B2);
  not not_8 (not_8_out, A2);
  not not_9 (not_9_out, A1);
  not not_10 (not_10_out, C2);
  not not_11 (not_11_out, A2);
  not not_12 (not_12_out, C1);
  not not_13 (not_13_out, B1);
  not not_14 (not_14_out, C1);
  not not_15 (not_15_out, A1);
  not not_16 (not_16_out, A1);
  not not_17 (not_17_out, C2);
  not not_18 (not_18_out, A2);
  not not_19 (not_19_out, C1);
  not not_20 (not_20_out, C2);
  not not_21 (not_21_out, B1);
  not not_22 (not_22_out, A1);
  not not_23 (not_23_out, A1);
  not not_24 (not_24_out, C1);
  not not_25 (not_25_out, B2);
  not not_26 (not_26_out, A1);
  not not_27 (not_27_out, B2);
  not not_28 (not_28_out, A2);
  not not_29 (not_29_out, C1);
  not not_30 (not_30_out, A1);
  not not_31 (not_31_out, B2);
  not not_32 (not_32_out, C2);
  not not_33 (not_33_out, A1);
  not not_34 (not_34_out, A2);
  and and_1 (and_1_out, not_1_out, C2, A2);
  and and_2 (and_2_out, not_2_out, C2, B2);
  and and_3 (and_3_out, C1, A1, not_3_out);
  and and_4 (and_4_out, C1, B1);
  and and_5 (and_5_out, not_4_out, not_5_out);
  and and_6 (and_6_out, C1, C2, B2);
  and and_7 (and_7_out, C1, A1, C2);
  and and_8 (and_8_out, C1, B1, A1);
  and and_9 (and_9_out, not_6_out, not_7_out, not_8_out);
  and and_10 (and_10_out, not_9_out, not_10_out, not_11_out);
  and and_11 (and_11_out, not_12_out, not_13_out, C2);
  and and_12 (and_12_out, not_14_out, B1, A1);
  and and_13 (and_13_out, C1, C2, B2);
  and and_14 (and_14_out, C1, B1, not_15_out);
  and and_15 (and_15_out, not_16_out, not_17_out, not_18_out);
  and and_16 (and_16_out, not_19_out, not_20_out, B2);
  and and_17 (and_17_out, not_21_out, not_22_out, C2, A2);
  and and_18 (and_18_out, B1, not_23_out, B2);
  and and_19 (and_19_out, not_24_out, B1, A1);
  and and_20 (and_20_out, C1, A1, C2, not_25_out);
  and and_21 (and_21_out, not_26_out, not_27_out, not_28_out);
  and and_22 (and_22_out, not_29_out, not_30_out, C2, A2);
  and and_23 (and_23_out, C2, not_31_out, A2);
  and and_24 (and_24_out, A1, not_32_out, A2);
  and and_25 (and_25_out, C1, not_33_out, not_34_out);
  and and_26 (and_26_out, C1, A1, A2);
  or or_1 (e, and_1_out, and_2_out, and_3_out, and_4_out);
  or or_2 (d, and_5_out, and_6_out, and_7_out, and_8_out);
  or or_3 (c, and_9_out, and_10_out, and_11_out, and_12_out, and_13_out, and_14_out);
  or or_4 (b, and_15_out, and_16_out, and_17_out, and_18_out, and_19_out, and_20_out);
  or or_5 (a, and_21_out, and_22_out, and_23_out, and_24_out, and_25_out, and_26_out);
endmodule

module salida (
  input  A,
  input  B,
  input  C,
  output [3:0] out_4
);

  wire and_1_out, and_2_out, and_3_out, and_4_out, not_1_out, not_2_out;

  not not_1 (not_1_out, B);
  not not_2 (not_2_out, C);
  and and_1 (and_1_out, not_1_out, not_2_out);
  and and_2 (and_2_out, B, not_2_out);
  and and_3 (and_3_out, B, C);
  and and_4 (and_4_out, not_1_out, C);
  or or_1 (out_4[3], and_1_out, A);
  or or_2 (out_4[2], A, and_2_out);
  or or_3 (out_4[1], A, and_3_out);
  or or_4 (out_4[0], A, and_4_out);

  // Notes on the sheet:
  //   a
  //   b
  //   c
  //   d
endmodule

module logicaEstados (
  input  [2:0] in_1,
  input  [2:0] in_2,
  input  [4:0] in_3,
  output [4:0] out_4,
  output out_5,
  output out_6,
  output out_7
);

  Coordenada_Codificacion coordenada_codificacion_1 (
    .cordenada_Y(in_2), .cordenada_X(in_1), .out_7(out_4[0]), .out_6(out_4[1]), .out_5(out_4[2]),
    .out_4(out_4[3]), .out_3(out_4[4]));
  direccion direccion_1 (.in_1(in_3), .complete(out_5), .dir(out_6), .s(out_7));
endmodule

module Logica_clock (
  input  in_1,
  input  in_2,
  input  in_3,
  output out_4
);

  wire not_1_out, not_2_out, or_1_out, or_2_out;

  and and_1 (out_4, or_1_out, or_2_out);
  or or_1 (or_1_out, not_1_out, in_3);
  not not_1 (not_1_out, in_2);
  not not_2 (not_2_out, in_1);
  or or_2 (or_2_out, not_2_out, not_1_out);
endmodule

module registro (
  input  in_1,
  input  [4:0] in_2,
  input  in_3,
  output [4:0] out_4
);

  FF_D ff_d_1 (.D(in_2[0]), .Q(out_4[0]), .Clk(in_1), .in_3(in_3));  // open: Not_Q
  FF_D ff_d_2 (.D(in_2[1]), .Q(out_4[1]), .Clk(in_1), .in_3(in_3));  // open: Not_Q
  FF_D ff_d_3 (.D(in_2[2]), .Q(out_4[2]), .Clk(in_1), .in_3(in_3));  // open: Not_Q
  FF_D ff_d_4 (.D(in_2[3]), .Q(out_4[3]), .Clk(in_1), .in_3(in_3));  // open: Not_Q
  FF_D ff_d_5 (.D(in_2[4]), .Q(out_4[4]), .Clk(in_1), .in_3(in_3));  // open: Not_Q
endmodule

module Comparar (
  input  [4:0] in_1,
  input  [4:0] in_2,
  output out_3
);

  wire [4:0] xor_1_out;

  assign xor_1_out = in_1 ^ in_2;  // XOR_Gate xor_1, 5 bits wide
  or or_1 (out_3, xor_1_out[0], xor_1_out[1], xor_1_out[2], xor_1_out[3], xor_1_out[4]);
endmodule

module FF_D (
  input  D,
  input  Clk,
  input  in_3,
  output Q,
  output Not_Q
);

  wire nand_1_out, nand_2_out, nand_3_out, nand_4_out, nand_5_out, nand_6_out, not_1_out;

  nand nand_1 (nand_1_out, D, Clk);
  not not_1 (not_1_out, Clk);
  nand nand_2 (nand_2_out, nand_1_out, Clk);
  nand nand_3 (nand_3_out, nand_1_out, 1'b1, nand_4_out);
  nand nand_4 (nand_4_out, nand_3_out, in_3, nand_2_out);
  nand nand_5 (nand_5_out, nand_3_out, not_1_out);
  nand nand_6 (nand_6_out, nand_5_out, not_1_out);
  nand nand_7 (Q, nand_5_out, 1'b1, Not_Q);
  nand nand_8 (Not_Q, Q, in_3, nand_6_out);

  // Notes on the sheet:
  //   Q: pull=down
  //   Not_Q: pull=up
  //   D: pull=down
  //   Clk: pull=up
endmodule
